// Logisim project corg-final.circ as structural Verilog: 4 circuits, main circuit main
module main (
  output [15:0] out_1
);

  wire and_1_out, and_2_out, and_3_out, and_4_out, and_5_out, and_6_out, and_7_out, and_8_out, and_9_out,
       and_10_out, and_11_out, and_12_out, and_13_out, and_14_out, and_15_out, and_16_out, clock_1_out, DEC,
       decoder_1_out0, decoder_1_out5, decoder_6_out0, decoder_6_out1, decoder_6_out2, decoder_6_out3,
       decoder_7_out0, decoder_7_out1, decoder_8_out0, decoder_8_out1, decoder_9_out0, decoder_9_out1,
       decoder_10_out0, decoder_10_out5, decoder_10_out6, decoder_10_out7, decoder_15_out0, decoder_15_out1,
       decoder_16_out0, decoder_16_out1, decoder_18_out0, decoder_18_out1, decoder_19_out0, decoder_19_out1,
       INC, IR_EN, IR_LH, IRTODST, LSSRC, MARTIRH, MARTIRL, MEM_CLR, MEM_LD, MEM_SEL, MEM_STR, MTDST,
       MuxCSel, NOT, not_1_out, not_2_out, not_3_out, not_4_out, not_5_out, not_6_out, not_7_out, not_8_out,
       not_9_out, not_10_out, not_11_out, not_12_out, or_4_out, RSSRC, SPTSRC, SRCTDST, SRCTOM, SRCTSP,
       tunnel;
  wire [1:0] _3RB_FS, _4RB_FS, controlled_buffer_10_out, controlled_buffer_23_out, controlled_buffer_32_out,
       controlled_buffer_49_out, controlled_buffer_53_out, controlled_buffer_58_out,
       controlled_buffer_61_out, controlled_buffer_62_out, controlled_buffer_64_out,
       controlled_buffer_68_out, controlled_buffer_86_out, controlled_buffer_94_out,
       controlled_buffer_95_out, controlled_buffer_100_out, controlled_buffer_103_out,
       controlled_buffer_105_out, controlled_buffer_106_out, controlled_buffer_110_out,
       controlled_buffer_111_out, controlled_buffer_119_out, controlled_buffer_120_out,
       controlled_buffer_121_out, controlled_buffer_126_out, IR_FS, MuxASel, MuxBSel, OutASel, OutBSel,
       OutCSel, OutDSel;
  wire [2:0] F1, F2, F3;
  wire [3:0] _3RB_RS, _4RB_RS, ALUFlags, ALUFS;

  assign OutDSel = SRCTSP ? 2'b10 : 2'bz;  // Controlled_Buffer controlled_buffer_1
  assign MEM_SEL = SRCTSP ? 1'b1 : 1'bz;  // Controlled_Buffer controlled_buffer_2
  assign MEM_LD = SRCTSP ? 1'b1 : 1'bz;  // Controlled_Buffer controlled_buffer_3
  assign MEM_STR = SRCTSP ? 1'b1 : 1'bz;  // Controlled_Buffer controlled_buffer_4
  assign MEM_CLR = SRCTSP ? 1'b0 : 1'bz;  // Controlled_Buffer controlled_buffer_5
  Decoder #(.select(3), .enable("false")) decoder_1 (
    .out0(decoder_1_out0), .out1(SRCTDST), .out2(MTDST), .out3(IRTODST), .out4(INC), .out5(decoder_1_out5),
    .out6(DEC), .out7(SRCTOM), .sel(F1));
  not not_1 (not_1_out, out_1[10]);
  and and_1 (and_1_out, SRCTDST, not_1_out, not_4_out);
  assign OutASel = and_1_out ? out_1[6:5] : 2'bz;  // Controlled_Buffer controlled_buffer_6
  assign MuxCSel = and_1_out ? 1'b1 : 1'bz;  // Controlled_Buffer controlled_buffer_7
  assign ALUFS = and_1_out ? 4'b0000 : 4'bz;  // Controlled_Buffer controlled_buffer_8
  assign MuxASel = and_1_out ? 2'b11 : 2'bz;  // Controlled_Buffer controlled_buffer_9
  Decoder #(.select(2), .disabled(0)) decoder_2 (
    .out0(_4RB_RS[0]), .out1(_4RB_RS[1]), .out2(_4RB_RS[2]), .out3(_4RB_RS[3]),
    .sel(controlled_buffer_10_out), .en(and_1_out));
  assign controlled_buffer_10_out = and_1_out ? out_1[9:8] : 2'bz;  // Controlled_Buffer controlled_buffer_10
  assign _4RB_FS = and_1_out ? 2'b01 : 2'bz;  // Controlled_Buffer controlled_buffer_11
  assign IR_EN = MARTIRL ? 1'b1 : 1'bz;  // Controlled_Buffer controlled_buffer_12
  assign MEM_SEL = MARTIRL ? 1'b1 : 1'bz;  // Controlled_Buffer controlled_buffer_13
  assign MEM_LD = MARTIRL ? 1'b1 : 1'bz;  // Controlled_Buffer controlled_buffer_14
  assign IR_FS = MARTIRL ? 2'b11 : 2'bz;  // Controlled_Buffer controlled_buffer_15
  assign IR_LH = MARTIRL ? 1'b0 : 1'bz;  // Controlled_Buffer controlled_buffer_16
  assign OutDSel = MARTIRL ? 2'b00 : 2'bz;  // Controlled_Buffer controlled_buffer_17
  assign _3RB_FS = MARTIRL ? 2'b10 : 2'bz;  // Controlled_Buffer controlled_buffer_18
  assign _3RB_RS = MARTIRL ? 4'b0001 : 4'bz;  // Controlled_Buffer controlled_buffer_19
  assign MEM_STR = MARTIRL ? 1'b0 : 1'bz;  // Controlled_Buffer controlled_buffer_20
  assign MEM_CLR = MARTIRL ? 1'b0 : 1'bz;  // Controlled_Buffer controlled_buffer_21
  not not_2 (not_2_out, out_1[10]);
  and and_2 (and_2_out, INC, not_2_out);
  assign _4RB_FS = and_2_out ? 2'b10 : 2'bz;  // Controlled_Buffer controlled_buffer_22
  assign controlled_buffer_23_out = and_2_out ? out_1[9:8] : 2'bz;  // Controlled_Buffer controlled_buffer_23
  assign OutASel = and_2_out ? out_1[9:8] : 2'bz;  // Controlled_Buffer controlled_buffer_24
  assign MuxCSel = and_2_out ? 1'b1 : 1'bz;  // Controlled_Buffer controlled_buffer_25
  assign OutDSel = MTDST ? 2'b01 : 2'bz;  // Controlled_Buffer controlled_buffer_26
  assign MEM_SEL = MTDST ? 1'b1 : 1'bz;  // Controlled_Buffer controlled_buffer_27
  assign MEM_LD = MTDST ? 1'b1 : 1'bz;  // Controlled_Buffer controlled_buffer_28
  assign MEM_STR = MTDST ? 1'b0 : 1'bz;  // Controlled_Buffer controlled_buffer_29
  assign MEM_CLR = MTDST ? 1'b0 : 1'bz;  // Controlled_Buffer controlled_buffer_30
  not not_3 (not_3_out, out_1[7]);
  and and_3 (and_3_out, NOT, not_3_out, not_5_out);
  assign OutASel = and_3_out ? out_1[6:5] : 2'bz;  // Controlled_Buffer controlled_buffer_31
  assign controlled_buffer_32_out = and_3_out ? out_1[9:8] : 2'bz;  // Controlled_Buffer controlled_buffer_32
  assign MuxCSel = and_3_out ? 1'b1 : 1'bz;  // Controlled_Buffer controlled_buffer_33
  assign ALUFS = and_3_out ? 4'b0010 : 4'bz;  // Controlled_Buffer controlled_buffer_34
  assign MuxASel = and_3_out ? 2'b11 : 2'bz;  // Controlled_Buffer controlled_buffer_35
  assign _4RB_FS = and_3_out ? 2'b01 : 2'bz;  // Controlled_Buffer controlled_buffer_36
  Clock clock_1 (.out(clock_1_out));
  CONTROL_UNIT control_unit_1 (
    .in_2(out_1[8]), .NEGATIVE_FLAG(ALUFlags[2]), .ZERO_FLAG(ALUFlags[3]), .OPCODE(out_1[15:11]), .F1(F1),
    .F3(F3), .in_1(clock_1_out), .F2(F2));
  not not_4 (not_4_out, out_1[7]);
  Decoder #(.select(2), .disabled(0)) decoder_3 (
    .out0(_4RB_RS[0]), .out1(_4RB_RS[1]), .out2(_4RB_RS[2]), .out3(_4RB_RS[3]),
    .sel(controlled_buffer_23_out), .en(and_2_out));
  and and_4 (and_4_out, SRCTSP, not_6_out);
  not not_5 (not_5_out, out_1[10]);
  Decoder #(.select(2), .disabled(0)) decoder_4 (
    .out0(_4RB_RS[0]), .out1(_4RB_RS[1]), .out2(_4RB_RS[2]), .out3(_4RB_RS[3]),
    .sel(controlled_buffer_32_out), .en(and_3_out));
  assign IR_EN = MARTIRH ? 1'b1 : 1'bz;  // Controlled_Buffer controlled_buffer_37
  assign MEM_SEL = MARTIRH ? 1'b1 : 1'bz;  // Controlled_Buffer controlled_buffer_38
  assign MEM_LD = MARTIRH ? 1'b1 : 1'bz;  // Controlled_Buffer controlled_buffer_39
  assign IR_FS = MARTIRH ? 2'b11 : 2'bz;  // Controlled_Buffer controlled_buffer_40
  assign IR_LH = MARTIRH ? 1'b1 : 1'bz;  // Controlled_Buffer controlled_buffer_41
  assign OutDSel = MARTIRH ? 2'b00 : 2'bz;  // Controlled_Buffer controlled_buffer_42
  assign _3RB_FS = MARTIRH ? 2'b10 : 2'bz;  // Controlled_Buffer controlled_buffer_43
  assign _3RB_RS = MARTIRH ? 4'b0001 : 4'bz;  // Controlled_Buffer controlled_buffer_44
  assign MEM_STR = MARTIRH ? 1'b0 : 1'bz;  // Controlled_Buffer controlled_buffer_45
  assign MEM_CLR = MARTIRH ? 1'b0 : 1'bz;  // Controlled_Buffer controlled_buffer_46
  assign MuxASel = MTDST ? 2'b01 : 2'bz;  // Controlled_Buffer controlled_buffer_47
  assign _4RB_FS = MTDST ? 2'b01 : 2'bz;  // Controlled_Buffer controlled_buffer_48
  assign controlled_buffer_49_out = MTDST ? out_1[10:9] : 2'bz;  // Controlled_Buffer controlled_buffer_49
  not not_6 (not_6_out, out_1[10]);
  assign OutASel = and_4_out ? out_1[9:8] : 2'bz;  // Controlled_Buffer controlled_buffer_50
  assign MuxCSel = and_4_out ? 1'b1 : 1'bz;  // Controlled_Buffer controlled_buffer_51
  assign ALUFS = and_4_out ? 4'b0000 : 4'bz;  // Controlled_Buffer controlled_buffer_52
  and and_5 (and_5_out, SRCTDST, out_1[10], out_1[7]);
  assign controlled_buffer_53_out = and_5_out ? out_1[6:5] : 2'bz;  // Controlled_Buffer controlled_buffer_53
  assign MuxASel = and_5_out ? 2'b10 : 2'bz;  // Controlled_Buffer controlled_buffer_54
  assign MuxCSel = and_5_out ? 1'b0 : 1'bz;  // Controlled_Buffer controlled_buffer_55
  assign ALUFS = and_5_out ? 4'b0000 : 4'bz;  // Controlled_Buffer controlled_buffer_56
  assign MuxBSel = and_5_out ? 2'b11 : 2'bz;  // Controlled_Buffer controlled_buffer_57
  assign controlled_buffer_58_out = and_5_out ? out_1[9:8] : 2'bz;  // Controlled_Buffer controlled_buffer_58
  assign _3RB_FS = and_5_out ? 2'b01 : 2'bz;  // Controlled_Buffer controlled_buffer_59
  Decoder #(.select(2), .disabled(0)) decoder_5 (
    .out0(_4RB_RS[0]), .out1(_4RB_RS[1]), .out2(_4RB_RS[2]), .out3(_4RB_RS[3]),
    .sel(controlled_buffer_49_out), .en(MTDST));
  not not_7 (not_7_out, out_1[7]);
  and and_6 (and_6_out, NOT, not_7_out, out_1[10]);
  Decoder #(.select(3), .enable("false")) decoder_6 (
    .out0(decoder_6_out0), .out1(decoder_6_out1), .out2(decoder_6_out2), .out3(decoder_6_out3), .out4(NOT),
    .out5(LSSRC), .out6(RSSRC), .out7(tunnel), .sel(F2));
  outcdecoder outcdecoder_1 (.in_1(controlled_buffer_53_out), .out_2(OutCSel));
  Decoder #(.select(2), .disabled(0)) decoder_7 (
    .out0(decoder_7_out0), .out1(decoder_7_out1), .out2(_3RB_RS[1]), .out3(_3RB_RS[2]),
    .sel(controlled_buffer_58_out), .en(and_5_out));
  or or_1 (_3RB_RS[0], decoder_7_out0, decoder_7_out1);
  and and_7 (and_7_out, INC, out_1[10]);
  assign _3RB_FS = and_7_out ? 2'b10 : 2'bz;  // Controlled_Buffer controlled_buffer_60
  Decoder #(.select(2), .disabled(0)) decoder_8 (
    .out0(decoder_8_out0), .out1(decoder_8_out1), .out2(_3RB_RS[1]), .out3(_3RB_RS[2]),
    .sel(controlled_buffer_61_out), .en(and_7_out));
  assign controlled_buffer_61_out = and_7_out ? out_1[9:8] : 2'bz;  // Controlled_Buffer controlled_buffer_61
  or or_2 (_3RB_RS[0], decoder_8_out0, decoder_8_out1);
  outcdecoder outcdecoder_2 (.in_1(controlled_buffer_62_out), .out_2(OutCSel));
  assign controlled_buffer_62_out = and_7_out ? out_1[9:8] : 2'bz;  // Controlled_Buffer controlled_buffer_62
  assign MuxCSel = and_7_out ? 1'b0 : 1'bz;  // Controlled_Buffer controlled_buffer_63
  and and_8 (and_8_out, SRCTSP, out_1[10]);
  assign controlled_buffer_64_out = and_8_out ? out_1[9:8] : 2'bz;  // Controlled_Buffer controlled_buffer_64
  assign MuxCSel = and_8_out ? 1'b0 : 1'bz;  // Controlled_Buffer controlled_buffer_65
  assign ALUFS = and_8_out ? 4'b0000 : 4'bz;  // Controlled_Buffer controlled_buffer_66
  assign OutASel = and_6_out ? out_1[6:5] : 2'bz;  // Controlled_Buffer controlled_buffer_67
  Decoder #(.select(2), .disabled(0)) decoder_9 (
    .out0(decoder_9_out0), .out1(decoder_9_out1), .out2(_3RB_RS[1]), .out3(_3RB_RS[2]),
    .sel(controlled_buffer_68_out), .en(and_6_out));
  assign controlled_buffer_68_out = and_6_out ? out_1[9:8] : 2'bz;  // Controlled_Buffer controlled_buffer_68
  or or_3 (_3RB_RS[0], decoder_9_out0, decoder_9_out1);
  assign MuxCSel = and_6_out ? 1'b1 : 1'bz;  // Controlled_Buffer controlled_buffer_69
  assign ALUFS = and_6_out ? 4'b0010 : 4'bz;  // Controlled_Buffer controlled_buffer_70
  assign MuxBSel = and_6_out ? 2'b11 : 2'bz;  // Controlled_Buffer controlled_buffer_71
  assign _3RB_FS = and_6_out ? 2'b01 : 2'bz;  // Controlled_Buffer controlled_buffer_72
  outcdecoder outcdecoder_3 (.in_1(controlled_buffer_64_out), .out_2(OutCSel));
  or or_4 (or_4_out, INC, DEC, NOT, LSSRC, RSSRC);
  assign OutDSel = or_4_out ? 2'b01 : 2'bz;  // Controlled_Buffer controlled_buffer_73
  assign MEM_SEL = or_4_out ? 1'b1 : 1'bz;  // Controlled_Buffer controlled_buffer_74
  assign MEM_LD = or_4_out ? 1'b1 : 1'bz;  // Controlled_Buffer controlled_buffer_75
  assign MEM_STR = or_4_out ? 1'b0 : 1'bz;  // Controlled_Buffer controlled_buffer_76
  assign MEM_CLR = or_4_out ? 1'b0 : 1'bz;  // Controlled_Buffer controlled_buffer_77
  and and_9 (and_9_out, DEC, not_8_out);
  assign OutBSel = SRCTOM ? out_1[10:9] : 2'bz;  // Controlled_Buffer controlled_buffer_78
  assign ALUFS = SRCTOM ? 4'b0001 : 4'bz;  // Controlled_Buffer controlled_buffer_79
  assign MEM_SEL = SRCTOM ? 1'b1 : 1'bz;  // Controlled_Buffer controlled_buffer_80
  assign MEM_LD = SRCTOM ? 1'b1 : 1'bz;  // Controlled_Buffer controlled_buffer_81
  assign MEM_STR = SRCTOM ? 1'b1 : 1'bz;  // Controlled_Buffer controlled_buffer_82
  assign MEM_CLR = SRCTOM ? 1'b0 : 1'bz;  // Controlled_Buffer controlled_buffer_83
  assign OutDSel = SRCTOM ? 2'b01 : 2'bz;  // Controlled_Buffer controlled_buffer_84
  part2_edited_main main_1 (
    .OutASel(OutASel), .OutBSel(OutBSel), .FunSel_2(_4RB_FS), .RegSel(_4RB_RS), .MuxASel(MuxASel),
    .OutCSel(OutCSel), .OutDSel(OutDSel), .FunSel_3(_3RB_FS), .RegSel_2(_3RB_RS), .L_H(IR_LH),
    .Enable(IR_EN), .FunSel_4(IR_FS), .MuxCSel(MuxCSel), .MuxBSel(MuxBSel), .FunSel(ALUFS), .in_10(MEM_STR),
    .in_11(MEM_SEL), .in_12(MEM_LD), .in_13(MEM_CLR), .out_22(ALUFlags), .out_23(out_1), .in_2(clock_1_out));  // open: out_21
  Decoder #(.select(3), .enable("false")) decoder_10 (
    .out0(decoder_10_out0), .out1(MARTIRL), .out2(MARTIRH), .out3(SRCTSP), .out4(SPTSRC),
    .out5(decoder_10_out5), .out6(decoder_10_out6), .out7(decoder_10_out7), .sel(F3));
  not not_8 (not_8_out, out_1[10]);
  assign _4RB_FS = and_9_out ? 2'b11 : 2'bz;  // Controlled_Buffer controlled_buffer_85
  Decoder #(.select(2), .disabled(0)) decoder_11 (
    .out0(_4RB_RS[0]), .out1(_4RB_RS[1]), .out2(_4RB_RS[2]), .out3(_4RB_RS[3]),
    .sel(controlled_buffer_86_out), .en(and_9_out));
  assign controlled_buffer_86_out = and_9_out ? out_1[9:8] : 2'bz;  // Controlled_Buffer controlled_buffer_86
  assign OutASel = and_9_out ? out_1[9:8] : 2'bz;  // Controlled_Buffer controlled_buffer_87
  assign MuxCSel = and_9_out ? 1'b1 : 1'bz;  // Controlled_Buffer controlled_buffer_88
  assign OutDSel = SPTSRC ? 2'b10 : 2'bz;  // Controlled_Buffer controlled_buffer_89
  assign MEM_SEL = SPTSRC ? 1'b1 : 1'bz;  // Controlled_Buffer controlled_buffer_90
  assign MEM_LD = SPTSRC ? 1'b1 : 1'bz;  // Controlled_Buffer controlled_buffer_91
  assign MEM_STR = SPTSRC ? 1'b0 : 1'bz;  // Controlled_Buffer controlled_buffer_92
  assign MEM_CLR = SPTSRC ? 1'b0 : 1'bz;  // Controlled_Buffer controlled_buffer_93
  and and_10 (and_10_out, NOT, out_1[7], not_10_out);
  assign controlled_buffer_94_out = and_10_out ? out_1[6:5] : 2'bz;  // Controlled_Buffer controlled_buffer_94
  outcdecoder outcdecoder_4 (.in_1(controlled_buffer_94_out), .out_2(OutCSel));
  Decoder #(.select(2), .disabled(0)) decoder_12 (
    .out0(_4RB_RS[0]), .out1(_4RB_RS[1]), .out2(_4RB_RS[2]), .out3(_4RB_RS[3]),
    .sel(controlled_buffer_95_out), .en(and_10_out));
  assign controlled_buffer_95_out = and_10_out ? out_1[9:8] : 2'bz;  // Controlled_Buffer controlled_buffer_95
  assign MuxCSel = and_10_out ? 1'b0 : 1'bz;  // Controlled_Buffer controlled_buffer_96
  assign ALUFS = and_10_out ? 4'b0010 : 4'bz;  // Controlled_Buffer controlled_buffer_97
  assign MuxASel = and_10_out ? 2'b11 : 2'bz;  // Controlled_Buffer controlled_buffer_98
  assign _4RB_FS = and_10_out ? 2'b01 : 2'bz;  // Controlled_Buffer controlled_buffer_99
  not not_9 (not_9_out, out_1[10]);
  and and_11 (and_11_out, not_9_out, out_1[7]);
  assign controlled_buffer_100_out = and_11_out ? out_1[6:5] : 2'bz;  // Controlled_Buffer controlled_buffer_100
  assign MuxASel = and_11_out ? 2'b10 : 2'bz;  // Controlled_Buffer controlled_buffer_101
  assign _4RB_FS = and_11_out ? 2'b01 : 2'bz;  // Controlled_Buffer controlled_buffer_102
  Decoder #(.select(2), .disabled(0)) decoder_13 (
    .out0(_4RB_RS[0]), .out1(_4RB_RS[1]), .out2(_4RB_RS[2]), .out3(_4RB_RS[3]),
    .sel(controlled_buffer_103_out), .en(and_11_out));
  assign controlled_buffer_103_out = and_11_out ? out_1[9:8] : 2'bz;  // Controlled_Buffer controlled_buffer_103
  not not_10 (not_10_out, out_1[10]);
  Hex_Digit_Display hex_digit_display_1 (.value(out_1[15:12]));  // open: dp
  outcdecoder outcdecoder_5 (.in_1(controlled_buffer_100_out), .out_2(OutCSel));
  and and_12 (and_12_out, SPTSRC, not_11_out);
  Hex_Digit_Display hex_digit_display_2 (.value(out_1[7:4]));  // open: dp
  Hex_Digit_Display hex_digit_display_3 (.value(out_1[11:8]));  // open: dp
  and and_13 (and_13_out, DEC, out_1[10]);
  assign _3RB_FS = and_13_out ? 2'b11 : 2'bz;  // Controlled_Buffer controlled_buffer_104
  assign controlled_buffer_105_out = and_13_out ? out_1[9:8] : 2'bz;  // Controlled_Buffer controlled_buffer_105
  assign controlled_buffer_106_out = and_13_out ? out_1[9:8] : 2'bz;  // Controlled_Buffer controlled_buffer_106
  assign MuxCSel = and_13_out ? 1'b0 : 1'bz;  // Controlled_Buffer controlled_buffer_107
  assign MuxASel = IRTODST ? 2'b00 : 2'bz;  // Controlled_Buffer controlled_buffer_108
  assign _4RB_FS = IRTODST ? 2'b01 : 2'bz;  // Controlled_Buffer controlled_buffer_109
  assign controlled_buffer_110_out = IRTODST ? out_1[10:9] : 2'bz;  // Controlled_Buffer controlled_buffer_110
  not not_11 (not_11_out, out_1[10]);
  Decoder #(.select(2), .disabled(0)) decoder_14 (
    .out0(_4RB_RS[0]), .out1(_4RB_RS[1]), .out2(_4RB_RS[2]), .out3(_4RB_RS[3]),
    .sel(controlled_buffer_111_out), .en(and_12_out));
  assign controlled_buffer_111_out = and_12_out ? out_1[9:8] : 2'bz;  // Controlled_Buffer controlled_buffer_111
  assign _4RB_FS = and_12_out ? 2'b01 : 2'bz;  // Controlled_Buffer controlled_buffer_112
  assign MuxASel = and_12_out ? 2'b01 : 2'bz;  // Controlled_Buffer controlled_buffer_113
  Hex_Digit_Display hex_digit_display_4 (.value(out_1[3:0]));  // open: dp
  and and_14 (and_14_out, SRCTDST, out_1[10], not_12_out);
  assign OutASel = and_14_out ? out_1[6:5] : 2'bz;  // Controlled_Buffer controlled_buffer_114
  assign MuxCSel = and_14_out ? 1'b1 : 1'bz;  // Controlled_Buffer controlled_buffer_115
  assign ALUFS = and_14_out ? 4'b0000 : 4'bz;  // Controlled_Buffer controlled_buffer_116
  assign MuxBSel = and_14_out ? 2'b11 : 2'bz;  // Controlled_Buffer controlled_buffer_117
  assign _3RB_FS = and_14_out ? 2'b01 : 2'bz;  // Controlled_Buffer controlled_buffer_118
  Decoder #(.select(2), .disabled(0)) decoder_15 (
    .out0(decoder_15_out0), .out1(decoder_15_out1), .out2(_3RB_RS[1]), .out3(_3RB_RS[2]),
    .sel(controlled_buffer_119_out), .en(and_14_out));
  assign controlled_buffer_119_out = and_14_out ? out_1[9:8] : 2'bz;  // Controlled_Buffer controlled_buffer_119
  or or_5 (_3RB_RS[0], decoder_15_out0, decoder_15_out1);
  Decoder #(.select(2), .disabled(0)) decoder_16 (
    .out0(decoder_16_out0), .out1(decoder_16_out1), .out2(_3RB_RS[1]), .out3(_3RB_RS[2]),
    .sel(controlled_buffer_105_out), .en(and_13_out));
  or or_6 (_3RB_RS[0], decoder_16_out0, decoder_16_out1);
  outcdecoder outcdecoder_6 (.in_1(controlled_buffer_106_out), .out_2(OutCSel));
  Decoder #(.select(2), .disabled(0)) decoder_17 (
    .out0(_4RB_RS[0]), .out1(_4RB_RS[1]), .out2(_4RB_RS[2]), .out3(_4RB_RS[3]),
    .sel(controlled_buffer_110_out), .en(IRTODST));
  and and_15 (and_15_out, NOT, out_1[7], out_1[10]);
  outcdecoder outcdecoder_7 (.in_1(controlled_buffer_120_out), .out_2(OutCSel));
  assign controlled_buffer_120_out = and_15_out ? out_1[6:5] : 2'bz;  // Controlled_Buffer controlled_buffer_120
  assign controlled_buffer_121_out = and_15_out ? out_1[9:8] : 2'bz;  // Controlled_Buffer controlled_buffer_121
  assign MuxCSel = and_15_out ? 1'b0 : 1'bz;  // Controlled_Buffer controlled_buffer_122
  assign ALUFS = and_15_out ? 4'b0010 : 4'bz;  // Controlled_Buffer controlled_buffer_123
  assign MuxBSel = and_15_out ? 2'b11 : 2'bz;  // Controlled_Buffer controlled_buffer_124
  assign _3RB_FS = and_15_out ? 2'b01 : 2'bz;  // Controlled_Buffer controlled_buffer_125
  not not_12 (not_12_out, out_1[7]);
  and and_16 (and_16_out, SPTSRC, out_1[10]);
  assign controlled_buffer_126_out = and_16_out ? out_1[9:8] : 2'bz;  // Controlled_Buffer controlled_buffer_126
  Decoder #(.select(2), .disabled(0)) decoder_18 (
    .out0(decoder_18_out0), .out1(decoder_18_out1), .out2(_3RB_RS[1]), .out3(_3RB_RS[2]),
    .sel(controlled_buffer_126_out), .en(and_16_out));
  or or_7 (_3RB_RS[0], decoder_18_out0, decoder_18_out1);
  assign _3RB_FS = and_16_out ? 2'b01 : 2'bz;  // Controlled_Buffer controlled_buffer_127
  assign MuxBSel = and_16_out ? 2'b10 : 2'bz;  // Controlled_Buffer controlled_buffer_128
  Decoder #(.select(2), .disabled(0)) decoder_19 (
    .out0(decoder_19_out0), .out1(decoder_19_out1), .out2(_3RB_RS[1]), .out3(_3RB_RS[2]),
    .sel(controlled_buffer_121_out), .en(and_15_out));
  or or_8 (_3RB_RS[0], decoder_19_out0, decoder_19_out1);

  // Other names for the same wires on the sheet: ADDRESS[7:0] = out_1[7:0]; INSTR[15:0] = out_1;
  //   SRCREG2[2:0] = out_1[4:2]; SRCREG1[2:0] = out_1[7:5]; AdrMOD = out_1[8]; DESTREG[2:0] = out_1[10:8];
  //   REGSEL[1:0] = out_1[10:9]; OPCODE[4:0] = out_1[15:11]

  // Notes on the sheet:
  //   MARTIRL
  //   MARTIRH
  //   INC
  //   MTDST
  //   SRCTSP
  //   SRCTODST
  //   NOT
  //   Memory Independent Operations
  //   SRCTOM
  //   DEC
  //   IRTODST
  //   SPTSRC
endmodule

module CONTROL_UNIT (
  input  in_1,
  input  in_2,
  input  NEGATIVE_FLAG,
  input  ZERO_FLAG,
  input  [4:0] OPCODE,
  output [2:0] F1,
  output [2:0] F2,
  output [2:0] F3
);

  wire and_1_out, and_2_out, and_3_out, and_4_out, decoder_1_out0, decoder_1_out1, decoder_1_out2,
       decoder_1_out3, multiplexer_1_out, not_1_out, not_2_out;
  wire [1:0] rom_1_data_3, rom_1_data_4;
  wire [2:0] rom_1_data;
  wire [7:0] adder_1_out, controlled_buffer_1_out, controlled_buffer_4_out, register_1_q, register_2_q,
       rom_1_data_2;
  wire [7:2] adder_2_out;

  not not_1 (not_1_out, multiplexer_1_out);
  and and_1 (and_1_out, decoder_1_out0, not_1_out);
  Adder adder_1 (.a(register_1_q), .b(8'h1), .out(adder_1_out));  // open: cin, cout
  assign controlled_buffer_1_out = and_1_out ? adder_1_out : 8'bz;  // Controlled_Buffer controlled_buffer_1
  and and_2 (and_2_out, decoder_1_out0, multiplexer_1_out);
  assign controlled_buffer_1_out = and_2_out ? rom_1_data_2 : 8'bz;  // Controlled_Buffer controlled_buffer_2
  and and_3 (and_3_out, decoder_1_out1, multiplexer_1_out);
  assign controlled_buffer_1_out = and_3_out ? rom_1_data_2 : 8'bz;  // Controlled_Buffer controlled_buffer_3
  assign controlled_buffer_4_out = and_3_out ? adder_1_out : 8'bz;  // Controlled_Buffer controlled_buffer_4
  not not_2 (not_2_out, multiplexer_1_out);
  and and_4 (and_4_out, decoder_1_out1, not_2_out);
  assign controlled_buffer_1_out = and_4_out ? adder_1_out : 8'bz;  // Controlled_Buffer controlled_buffer_5
  Register register_1 (.D(controlled_buffer_1_out), .Q(register_1_q), .clk(in_1));  // open: en, clr
  Register register_2 (.D(controlled_buffer_4_out), .en(and_3_out), .Q(register_2_q), .clk(in_1));  // open: clr
  assign controlled_buffer_1_out = decoder_1_out2 ? register_2_q : 8'bz;  // Controlled_Buffer controlled_buffer_6
  assign controlled_buffer_1_out = decoder_1_out3 ? {adder_2_out, 2'b00} : 8'bz;  // Controlled_Buffer controlled_buffer_7
  ROM #(.dataWidth(24)) rom_1 (
    .addr(register_1_q), .data({F1, F2, F3, rom_1_data_4, rom_1_data_3, rom_1_data_2, rom_1_data}));  // open: sel
  Decoder #(.select(2), .enable("false")) decoder_1 (
    .out0(decoder_1_out0), .out1(decoder_1_out1), .out2(decoder_1_out2), .out3(decoder_1_out3),
    .sel(rom_1_data_3));
  Multiplexer #(.select(2), .enable("false")) multiplexer_1 (
    .in0(1'b1), .in1(in_2), .in2(NEGATIVE_FLAG), .in3(ZERO_FLAG), .out(multiplexer_1_out), .sel(rom_1_data_4));
  Adder #(.width(5)) adder_2 (.a(OPCODE), .b(5'b00001), .out(adder_2_out[6:2]), .cout(adder_2_out[7]));  // open: cin

  // Notes on the sheet:
  //   Control Unit
  //   CAR
  //   SP
  //   Control Memory
  //   contents of rom_1 (hex, n*v repeats v):
  //   8008 10010 1800 0 402030 602030 800 0 e00048 800 0 0 200068 800 18*0 200108 c00000 0 0 200128 800000
  //   10*0 100000 0 0 0 140000 0 0 0 180000
  //   IR LOW PLACEHOLDER
endmodule

module outcdecoder (
  input  [1:0] in_1,
  output [1:0] out_2
);

  Subtractor #(.width(2)) subtractor_1 (.a(in_1), .b(2'b01), .out(out_2));  // open: bin, bout
endmodule

module converter (
  input  [4:0] OPCode,
  input  [1:0] RegSel,
  input  Adressing_Mode,
  input  [7:0] Address,
  input  Type_1,
  input  [4:0] OPCode_2,
  input  [2:0] DestReg,
  input  [2:0] SrcReg1,
  input  [2:0] SrcReg2,
  input  [2:0] F1,
  input  [2:0] F2,
  input  [2:0] F3,
  input  [1:0] CD,
  input  [2:0] FILLER,
  input  [1:0] BR,
  input  [7:0] AD
);

  wire not_1_out;
  wire [15:0] controlled_buffer_1_out;

  assign controlled_buffer_1_out = Type_1 ? {OPCode, RegSel, Adressing_Mode, Address} : 16'bz;  // Controlled_Buffer controlled_buffer_1
  not not_1 (not_1_out, Type_1);
  assign controlled_buffer_1_out = not_1_out ? {OPCode_2, DestReg, SrcReg1, SrcReg2, 2'b00} : 16'bz;  // Controlled_Buffer controlled_buffer_2
  // Probe on controlled_buffer_1_out[15:8]
  // Probe on controlled_buffer_1_out[7:0]
  // Probe on {F1, F2, F3, CD, BR, AD, FILLER}
endmodule
